# Fritzing sketch Circuit (saved by Fritzing 0.9.3b)
breadboards: 2

parts:
  LCD1 = LCD screen
  Bauteil1 = Arduino Uno (Rev3)
  hc-sr1 = hc-sr04
  R1 = Rotary Potentiometer (Small) [maximum_resistance=100kΩ package=THT]
  Bauteil2 = IR Receiver Breakout [package=PCB]
  Q1 = TRANSISTOR_NPN [package=to-92]
  Q2 = TRANSISTOR_NPN [package=to-92]

nets:
  GND: LCD1.VSS, LCD1.R/W, Bauteil1.GND, hc-sr1.GND, R1.leg1, Bauteil2.GND, Q1.C, Q2.E
  VDD: LCD1.VDD, LCD1.LED+, Bauteil1.5V, R1.leg2, Bauteil2.OUT
  N1: LCD1.V0, R1.wiper
  N2: LCD1.RS, Bauteil1.D12/MISO
  N3: LCD1.E, Bauteil1.D11_PWM/MOSI
  N4: LCD1.DB4, Bauteil1.D5_PWM
  N5: LCD1.DB5, Bauteil1.D4
  N6: LCD1.DB6, Bauteil1.D3_PWM
  N7: LCD1.DB7, Bauteil1.D2
  N8: LCD1.LED-, Bauteil1.D13/SCK
  N9: Bauteil1.D8, Q1.B
  N10: Bauteil1.D9_PWM, Q2.B
  N11: Bauteil1.D10_PWM/SS, Bauteil2.VCC
  N12: Bauteil1.D6_PWM, hc-sr1.Echo
  N13: Bauteil1.D7, hc-sr1.Trig

notes:
  bekant-controller
  UP GND DOWN
